# Fritzing sketch MFEx_WiringDiagram (saved by Fritzing 0.9.5d)

parts:
  S1 = Round Pushbutton
  Part1 = Arduino Nano (Rev3.0) (ICSP)
  S2 = Round Pushbutton
  S3 = Round Pushbutton
  S4 = Square Pushbutton
  HLK-PM1 = HLK-PM01
  M2 = ESC
  920KV_Motor2 = DJI 920 KV Motor  # not connected
  Part2 = LCD1602-I2C
  RY1 = SSR-40VA
  M3 = 1 chan 5v relay module

nets:
  GND: S1.leg0, Part1.GND, S2.leg0, S3.leg0, M2.GND, Part2.GND, RY1.Pin_4, M3.pin_3
  N1: S1.leg1, Part1.D6
  N2: Part1.D3, M2.DATA
  N3: Part1.D4, S3.leg1
  N4: Part1.D5, S2.leg1
  N5: Part1.D7, M3.pin_2
  N6: Part1.D9, RY1.Pin_3
  5V: Part1.5V, Part2.VCC, M3.pin_1
  N7: Part1.A5, Part2.SCL
  N8: Part1.A4, Part2.SDA
  N9: S4.leg1, HLK-PM1.AC#0

custom parts:
  DJI 920 KV Motor: DJI Brushless Outrunner 2212/920K Motor F330-550
  LCD1602-I2C: A standard character display, usually with 2x16 characters. Comes in many colors with LCM1602 IIC attached.
  SSR-40VA: SSR-40VA solid state relay.
  1 chan 5v relay module: 1 Channel 5V Relay Module Board Shield with Optocoupler Support High and Low Level Trigger for Arduino.
